# Fritzing sketch ALDL-reader-schematic (saved by Fritzing 1.0.5)
breadboards: 1

parts:
  MCU1 = Arduino Mega 2560 (Rev3)
  S5 = Toggle Switch [package=THT]
  S6 = Toggle Switch [package=THT]
  LCD1 = LCD screen
  D1 = Rectifier Diode [part_number=1N4001 package="Melf DO-213 AB [SMD]"]
  S1 = Round Pushbutton
  S2 = Round Pushbutton
  S3 = Round Pushbutton
  S4 = Round Pushbutton
  R1 = TRIMPOT [maximum_resistance=10kΩ knob_status=50% power=0.5W package=trimpot_tc33]
  R2 = Resistor [tolerance=±5% power=0.25W resistance=270 package=THT]
  JP1 = Header 2 [package=jst-2-pth-kit]
  LED1 = RGB LED - (4 legs) [color="Red (633nm)" current=0.030A package="5 mm [THT]"]
  R3 = Resistor [tolerance=±5% power=0.25W resistance=10k package=THT]
  R4 = Resistor [tolerance=±5% power=0.25W resistance=330 package=THT]
  R5 = Resistor [tolerance=±5% power=0.25W resistance=180 package=THT]
  JP2 = Header 3 [package=1x03-1mm-ra]

nets:
  N1: MCU1.D19/RX1, MCU1.D4_PWM, D1.anode, JP2.3
  N2: MCU1.D18/TX1, D1.cathode
  N3: MCU1.D12_PWM, LCD1.RS
  N4: MCU1.D11_PWM, LCD1.E
  N5: MCU1.D10_PWM, S1.leg1
  N6: MCU1.D9_PWM, S2.leg1
  N7: MCU1.D8_PWM, S3.leg1
  5V: MCU1.5V, LCD1.VDD, LCD1.LED+, R1.CW, LED1.common_anode
  N8: MCU1.VIN, S5.L2
  N9: MCU1.D2_PWM, LCD1.DB7
  N10: MCU1.D3_PWM, LCD1.DB6
  N11: MCU1.D5_PWM, LCD1.DB4
  N12: MCU1.D6_PWM, LCD1.DB5
  N13: MCU1.D7_PWM, S4.leg1
  N14: MCU1.D22, R4.Pin_1
  N15: MCU1.D24, R5.Pin_1
  N16: MCU1.D26, R2.Pin_1
  N17: S5.COM, JP1.2
  GND: S6.COM, LCD1.VSS, LCD1.LED-, S1.leg0, S2.leg0, S3.leg0, S4.leg0, R1.CCW, JP1.1, JP2.1
  N18: S6.L2, R3.Pin_1
  N19: LCD1.V0, R1.WIPER
  N20: R2.Pin_0, LED1.green_cathode
  N21: LED1.red_cathode, R4.Pin_0
  N22: LED1.blue_cathode, R5.Pin_0
  N23: R3.Pin_0, JP2.2

notes:
  20x4 text LCD
  ALDL plug
  1=A
  2=B
  3=E
  Cigarette lighter plug
